// Logisim project CLA.circ as structural Verilog: 2 circuits, main circuit main
module main (
  input  A0,
  input  B0,
  input  A1,
  input  B1,
  input  A2,
  input  B2,
  output S0,
  output S1,
  output S2,
  output S3,
  output C3
);

  wire and_1_out, and_2_out, and_3_out, carry_generate_1_c2, xor_2_out, xor_3_out;

  xor xor_1 (S0, A0, B0);
  and and_1 (and_1_out, A0, B0);
  xor xor_2 (xor_2_out, A1, B1);
  and and_2 (and_2_out, A1, B1);
  xor xor_3 (xor_3_out, A2, B2);
  and and_3 (and_3_out, A2, B2);
  Carry_Generate carry_generate_1 (
    .P2(xor_3_out), .G2(and_3_out), .P1(xor_2_out), .G1(and_2_out), .C1(and_1_out), .C3(S3),
    .C2(carry_generate_1_c2));  // open: P3, G3, C4
  xor xor_4 (S1, and_1_out, xor_2_out);
  xor xor_5 (S2, carry_generate_1_c2, xor_3_out);

  // Notes on the sheet:
  //   P0
  //   G0
  //   P1
  //   G1
  //   P2
  //   G2
endmodule

module Carry_Generate (
  input  P3,
  input  G3,
  input  P2,
  input  G2,
  input  P1,
  input  G1,
  input  C1,
  output C4,
  output C3,
  output C2
);

  wire and_1_out, and_2_out, and_3_out, and_4_out, and_5_out, and_6_out;

  and and_1 (and_1_out, P1, P2, P3, C1);
  and and_2 (and_2_out, G1, P2, P3);
  and and_3 (and_3_out, G2, P3);
  and and_4 (and_4_out, P1, P2, C1);
  and and_5 (and_5_out, G1, P2);
  and and_6 (and_6_out, P1, C1);
  or or_1 (C4, and_1_out, and_2_out, and_3_out, G3);
  or or_2 (C3, and_4_out, and_5_out, G2);
  or or_3 (C2, and_6_out, G1);

  // Notes on the sheet:
  //   Generates up to 4 carries
endmodule
