// Logisim project Full_Adder.circ as structural Verilog: 1 circuit, main circuit main
module main (
  input  A,
  input  A_2,
  input  B,
  input  B_2,
  input  Cin,
  input  Cin_2,
  output S,
  output S_2,
  output Cout,
  output Cout_2
);

  wire and_1_out, and_2_out, and_3_out, and_4_out, and_5_out, and_6_out, xor_2_out;

  xor xor_1 (S, A_2, B_2, Cin_2);
  and and_1 (and_1_out, A_2, B_2);
  and and_2 (and_2_out, A_2, Cin_2);
  and and_3 (and_3_out, B_2, Cin_2);
  or or_1 (Cout_2, and_1_out, and_2_out, and_3_out);
  xor xor_2 (xor_2_out, A, B);
  and and_4 (and_4_out, A, B);
  and and_5 (and_5_out, A, Cin);
  and and_6 (and_6_out, B, Cin);
  xor xor_3 (S_2, xor_2_out, Cin);
  or or_2 (Cout, and_4_out, and_5_out, and_6_out);

  // Notes on the sheet:
  //   Full Adder with 1 XOR
  //   Full Adder with 2 XOR
endmodule
