// Logisim project RCA.circ as structural Verilog: 1 circuit, main circuit main
module main (
  input  A0,
  input  B0,
  input  C0,
  input  A1,
  input  B1,
  input  A2,
  input  B2,
  output S0,
  output S1,
  output S2,
  output C3
);

  wire and_1_out, and_2_out, and_3_out, and_4_out, and_5_out, and_6_out, and_7_out, and_8_out, and_9_out,
       or_1_out, or_2_out;

  xor xor_1 (S0, A0, B0, C0);
  and and_1 (and_1_out, A0, B0);
  and and_2 (and_2_out, A0, C0);
  and and_3 (and_3_out, B0, C0);
  or or_1 (or_1_out, and_1_out, and_2_out, and_3_out);
  xor xor_2 (S1, A1, B1, or_1_out);
  and and_4 (and_4_out, A1, B1);
  and and_5 (and_5_out, A1, or_1_out);
  and and_6 (and_6_out, B1, or_1_out);
  or or_2 (or_2_out, and_4_out, and_5_out, and_6_out);
  xor xor_3 (S2, A2, B2, or_2_out);
  and and_7 (and_7_out, A2, B2);
  and and_8 (and_8_out, A2, or_2_out);
  and and_9 (and_9_out, B2, or_2_out);
  or or_3 (C3, and_7_out, and_8_out, and_9_out);
endmodule
