// Logisim project ComparatorExample.circ as structural Verilog: 3 circuits, main circuit main
module main (
  input  A0,
  input  B0,
  input  in_3,
  input  in_4,
  input  in_5,
  input  A1,
  input  B1,
  input  A2,
  input  B2,
  output out_10,
  output out_11,
  output out_12
);

  wire bitslicecomparator_1_eqo, bitslicecomparator_1_gto, bitslicecomparator_1_lto,
       bitslicecomparator_2_eqo, bitslicecomparator_2_gto, bitslicecomparator_2_lto, not_1_out, not_2_out;

  not not_1 (not_1_out, A2);
  not not_2 (not_2_out, B2);
  BitSliceComparator bitslicecomparator_1 (
    .A(A0), .B(B0), .GTi(in_3), .LTi(in_4), .EQi(in_5), .GTo(bitslicecomparator_1_gto),
    .LTo(bitslicecomparator_1_lto), .EQo(bitslicecomparator_1_eqo));
  BitSliceComparator bitslicecomparator_2 (
    .A(A1), .B(B1), .GTi(bitslicecomparator_1_gto), .LTi(bitslicecomparator_1_lto),
    .EQi(bitslicecomparator_1_eqo), .GTo(bitslicecomparator_2_gto), .LTo(bitslicecomparator_2_lto),
    .EQo(bitslicecomparator_2_eqo));
  BitSliceComparator bitslicecomparator_3 (
    .A(not_1_out), .B(not_2_out), .GTi(bitslicecomparator_2_gto), .LTi(bitslicecomparator_2_lto),
    .EQi(bitslicecomparator_2_eqo), .GTo(out_10), .LTo(out_11), .EQo(out_12));
endmodule

module BitSliceComparator (
  input  A,
  input  B,
  input  GTi,
  input  LTi,
  input  EQi,
  output GTo,
  output LTo,
  output EQo
);

  wire and_1_out, and_2_out, and_4_out, and_5_out, not_1_out, not_2_out, not_3_out, not_4_out, not_5_out,
       not_6_out, not_7_out, not_8_out, not_9_out, xor_1_out;

  xor xor_1 (xor_1_out, A, B);
  not not_1 (not_1_out, xor_1_out);
  not not_2 (not_2_out, LTi);
  not not_3 (not_3_out, EQi);
  not not_4 (not_4_out, GTi);
  not not_5 (not_5_out, EQi);
  not not_6 (not_6_out, GTi);
  not not_7 (not_7_out, LTi);
  not not_8 (not_8_out, B);
  not not_9 (not_9_out, A);
  and and_1 (and_1_out, GTi, not_2_out, not_3_out, not_1_out);
  and and_2 (and_2_out, not_4_out, LTi, not_5_out, not_1_out);
  and and_3 (EQo, not_6_out, not_7_out, EQi, not_1_out);
  and and_4 (and_4_out, A, not_8_out);
  and and_5 (and_5_out, not_9_out, xor_1_out, B);
  or or_1 (LTo, and_5_out, and_2_out);
  or or_2 (GTo, and_4_out, and_1_out);
endmodule

module Test (
  input  in_1,
  input  in_2,
  input  in_3,
  input  in_4,
  input  in_5,
  input  in_6,
  input  in_7,
  input  in_8,
  output out_9,
  output out_10,
  output out_11
);

  wire and_1_out, bitslicecomparator_1_eqo, bitslicecomparator_1_gto, bitslicecomparator_2_eqo,
       bitslicecomparator_2_gto, bitslicecomparator_3_eqo, bitslicecomparator_3_gto, not_1_out, xnor_1_out,
       xor_1_out, xor_2_out, xor_3_out, xor_4_out;

  and and_1 (and_1_out, in_7, in_8);
  xor xor_1 (xor_1_out, in_1, and_1_out);
  xor xor_2 (xor_2_out, in_2, and_1_out);
  xor xor_3 (xor_3_out, in_5, and_1_out);
  xor xor_4 (xor_4_out, in_6, and_1_out);
  BitSliceComparator bitslicecomparator_1 (
    .A(xor_1_out), .B(xor_2_out), .GTi(in_3), .EQi(in_4), .GTo(bitslicecomparator_1_gto),
    .EQo(bitslicecomparator_1_eqo));  // open: LTi, LTo
  BitSliceComparator bitslicecomparator_2 (
    .A(xor_3_out), .B(xor_4_out), .GTi(bitslicecomparator_1_gto), .EQi(bitslicecomparator_1_eqo),
    .GTo(bitslicecomparator_2_gto), .EQo(bitslicecomparator_2_eqo));  // open: LTi, LTo
  and and_2 (out_9, in_7, not_1_out);
  not not_1 (not_1_out, in_8);
  BitSliceComparator bitslicecomparator_3 (
    .A(in_7), .B(in_8), .GTi(bitslicecomparator_2_gto), .EQi(bitslicecomparator_2_eqo),
    .GTo(bitslicecomparator_3_gto), .EQo(bitslicecomparator_3_eqo));  // open: LTi, LTo
  xnor xnor_1 (xnor_1_out, in_8, in_7);
  and and_3 (out_9, bitslicecomparator_3_gto, xnor_1_out);
  and and_4 (out_11, bitslicecomparator_3_eqo, xnor_1_out);
  nor nor_1 (out_10, out_11, out_9);
endmodule
