// Logisim project D-Latch.circ as structural Verilog: 1 circuit, main circuit main
module main (
  input  D,
  input  G,
  output Q,
  output Q_N
);

  wire nand_1_out, nand_2_out;

  nand nand_1 (nand_1_out, D, G);
  nand nand_2 (nand_2_out, G, ~D);  // NAND_Gate
  or or_1 (Q, ~nand_1_out, ~Q_N);  // OR_Gate
  nand nand_3 (Q_N, Q, nand_2_out);
endmodule
