// Logisim project Dragon_RealFlyer.circ as structural Verilog: 1 circuit, main circuit main
module main (
  input  Y,
  input  A,
  input  W,
  input  in_4,
  input  O,
  input  N,
  output out_7
);

  wire and_2_out, or_1_out, undriven;

  and and_1 (out_7, Y, A, W);
  and and_2 (and_2_out, W, undriven);
  or or_1 (or_1_out, out_7, and_2_out);
endmodule
