// Logisim project Exams.circ as structural Verilog
module Exam2_p1 (
  input  A,
  input  B,
  input  C,
  output f1,
  output f2
);

  wire and_1_out, and_2_out, and_3_out, and_4_out, and_5_out, and_6_out, and_7_out, not_1_out, not_2_out,
       not_3_out, not_4_out, not_5_out, not_6_out;

  and and_1 (and_1_out, B, C);
  and and_2 (and_2_out, A, C);
  and and_3 (and_3_out, A, B);
  not not_1 (not_1_out, A);
  not not_2 (not_2_out, B);
  not not_3 (not_3_out, A);
  not not_4 (not_4_out, C);
  not not_5 (not_5_out, B);
  not not_6 (not_6_out, C);
  or or_1 (f1, and_1_out, and_2_out, and_3_out);
  and and_4 (and_4_out, not_1_out, not_2_out, C);
  and and_5 (and_5_out, not_3_out, B, not_4_out);
  and and_6 (and_6_out, A, not_5_out, not_6_out);
  and and_7 (and_7_out, A, B, C);
  or or_2 (f2, and_4_out, and_5_out, and_6_out, and_7_out);
endmodule

module Exam2_p2 (
  input  A,
  input  B,
  input  C,
  input  A_2,
  input  B_2,
  input  C_2,
  output F,
  output F_2
);

  wire and_1_out, and_2_out, not_1_out, not_2_out, or_1_out, or_2_out;

  and and_1 (and_1_out, B_2, A_2);
  and and_2 (and_2_out, A, B);
  or or_1 (or_1_out, ~A, C);  // OR_Gate
  or or_2 (or_2_out, ~and_1_out, C_2);  // OR_Gate
  not not_1 (not_1_out, or_1_out);
  not not_2 (not_2_out, or_2_out);
  and and_3 (F, and_2_out, not_1_out);
  or or_3 (F_2, A_2, B_2, not_2_out);
endmodule
