// Logisim project First Circuit.circ as structural Verilog: 1 circuit, main circuit main
module main (
  input  in_1,
  input  in_2,
  input  in_3
);

  wire and_1_out, and_2_out, nand_1_out;

  and and_1 (and_1_out, ~in_1, in_2);  // AND_Gate
  and and_2 (and_2_out, in_3, in_2);
  nand nand_1 (nand_1_out, and_1_out, and_2_out);
endmodule
