// Logisim project Morkie_Cookie.circ as structural Verilog: 1 circuit, main circuit main
module main (
  input  in_1,
  input  in_2,
  input  in_3,
  input  in_4,
  output out_5,
  output out_6
);

  wire and_1_out, and_2_out, or_1_out, or_2_out;

  or or_1 (or_1_out, in_1, in_2);
  or or_2 (or_2_out, in_3, in_4);
  and and_1 (and_1_out, in_2, in_3);
  and and_2 (and_2_out, in_1, in_4);
  and and_3 (out_5, or_1_out, or_2_out);
  or or_3 (out_6, and_1_out, and_2_out);
endmodule
