// Logisim project MultiplierExample.circ as structural Verilog: 5 circuits, main circuit MultiplerVersion1
module main (
  input  B0,
  input  B1,
  input  B2,
  input  A0,
  input  A1,
  input  A2,
  output F0,
  output F1,
  output F2,
  output F3,
  output F4,
  output F5
);

  wire and_2_out, and_3_out, and_4_out, and_5_out, and_6_out, and_7_out, and_8_out, and_9_out, fa_1_cout,
       fa_1_s, fa_2_cout, fa_2_s, ha_1_p4, ha_2_p4, ha_3_p1;

  and and_1 (F0, A0, B0);
  and and_2 (and_2_out, A1, B0);
  and and_3 (and_3_out, A2, B0);
  and and_4 (and_4_out, A0, B1);
  and and_5 (and_5_out, A1, B1);
  and and_6 (and_6_out, A2, B1);
  and and_7 (and_7_out, A0, B2);
  and and_8 (and_8_out, A1, B2);
  and and_9 (and_9_out, A2, B2);
  // HA ha_1: pin names not known; wires that end beside it: and_2_out, and_4_out, F1, ha_1_p4
  FA fa_1 (.S(fa_1_s), .Cout(fa_1_cout));  // open: A, B, Cin
  // HA ha_2: pin names not known; wires that end beside it: fa_1_s, and_7_out, F2, ha_2_p4
  FA fa_2 (.S(fa_2_s), .Cout(fa_2_cout));  // open: A, B, Cin
  // HA ha_3: pin names not known; wires that end beside it: ha_3_p1, and_9_out, F4, F5
  FA fa_3 (.S(F3), .Cout(ha_3_p1));  // open: A, B, Cin
endmodule

module FA (
  input  A,
  input  B,
  input  Cin,
  output S,
  output Cout
);

  wire and_1_out, and_2_out, and_3_out;

  xor xor_1 (S, A, B, Cin);
  and and_1 (and_1_out, A, B);
  and and_2 (and_2_out, A, Cin);
  and and_3 (and_3_out, B, Cin);
  or or_1 (Cout, and_1_out, and_2_out, and_3_out);
endmodule

module HA (
  input  A,
  input  B,
  output S,
  output Cout
);

  xor xor_1 (S, A, B);
  and and_1 (Cout, A, B);
endmodule

module Mult (
  input  B0,
  input  B1,
  input  B2,
  input  A0,
  input  A1,
  input  A2,
  output A0B0,
  output A0B1,
  output A0B2,
  output A1B0,
  output A1B1,
  output A1B2,
  output A2B0,
  output A2B1,
  output A2B2
);

  and and_1 (A0B0, A0, B0);
  and and_2 (A1B0, A1, B0);
  and and_3 (A2B0, A2, B0);
  and and_4 (A0B1, A0, B1);
  and and_5 (A1B1, A1, B1);
  and and_6 (A2B1, A2, B1);
  and and_7 (A0B2, A0, B2);
  and and_8 (A1B2, A1, B2);
  and and_9 (A2B2, A2, B2);
endmodule

module MultiplerVersion1 (
  input  B0,
  input  B1,
  input  B2,
  input  A0,
  input  A1,
  input  A2,
  output f0,
  output f1,
  output f2,
  output f3,
  output f4,
  output f5
);

  wire fa_1_cout, fa_1_s, fa_2_cout, fa_2_s, ha_1_cout, ha_2_cout, ha_3_cout, mult_1_a0b1, mult_1_a0b2,
       mult_1_a1b0, mult_1_a1b1, mult_1_a1b2, mult_1_a2b0, mult_1_a2b1, mult_1_a2b2;

  Mult mult_1 (
    .B0(B0), .B1(B1), .B2(B2), .A0(A0), .A1(A1), .A2(A2), .A0B0(f0), .A0B1(mult_1_a0b1), .A0B2(mult_1_a0b2),
    .A1B0(mult_1_a1b0), .A1B1(mult_1_a1b1), .A1B2(mult_1_a1b2), .A2B0(mult_1_a2b0), .A2B1(mult_1_a2b1),
    .A2B2(mult_1_a2b2));
  HA ha_1 (.A(mult_1_a0b1), .B(mult_1_a1b0), .S(f1), .Cout(ha_1_cout));
  FA fa_1 (.A(ha_1_cout), .B(mult_1_a1b1), .Cin(mult_1_a2b0), .S(fa_1_s), .Cout(fa_1_cout));
  HA ha_2 (.A(fa_1_s), .B(mult_1_a0b2), .S(f2), .Cout(ha_2_cout));
  FA fa_2 (.A(fa_1_cout), .B(ha_2_cout), .Cin(mult_1_a2b1), .S(fa_2_s), .Cout(fa_2_cout));
  HA ha_3 (.A(fa_2_s), .B(mult_1_a1b2), .S(f3), .Cout(ha_3_cout));
  FA fa_3 (.A(ha_3_cout), .B(fa_2_cout), .Cin(mult_1_a2b2), .S(f4), .Cout(f5));

  // Notes on the sheet:
  //   +
  //   A2  A1  A0
  //   B2  B1  B0
  //   x
  //   C2  C1  C0
  //   D3  D2  D1
  //   E4  E3  E2
  //   f5    f4    f3    f2   f1   f0
  //   D2
  //   C2
  //   E2
  //   D3
  //   E3
  //   Carry
  //   E4
  //   Carry - A binary digit that moves to a higher significance (higher bit) ex. 1+1 = 1 1
  //   Carry
  //   Carry
  //   Carry
  //   Carry
endmodule
