// Logisim project Quiz1.circ as structural Verilog: 1 circuit, main circuit main
module main (
  input  x3,
  input  x2,
  input  x1,
  input  x0,
  input  in_5,
  input  in_6,
  input  in_7,
  input  in_8,
  input  in_9,
  input  in_10,
  input  in_11,
  input  in_12,
  output out_13,
  output out_14,
  output out_15
);

  wire and_1_out, and_2_out, nor_1_out, nor_2_out, nor_3_out, nor_4_out, nor_5_out, nor_6_out, nor_7_out,
       nor_8_out, nor_9_out, not_1_out, not_2_out;

  not not_1 (not_1_out, in_8);
  nor nor_1 (nor_1_out, x0, x1);
  nor nor_2 (nor_2_out, in_8, in_7);
  not not_2 (not_2_out, in_8);
  nor nor_3 (nor_3_out, in_12, in_11);
  and and_1 (and_1_out, nor_1_out, ~x0);  // AND_Gate
  and and_2 (and_2_out, ~x0, x2);  // AND_Gate
  nor nor_4 (nor_4_out, ~not_1_out, ~in_6);  // NOR_Gate
  nor nor_5 (nor_5_out, in_12, ~in_10);  // NOR_Gate
  nor nor_6 (nor_6_out, ~nor_2_out, ~not_2_out);  // NOR_Gate
  nor nor_7 (nor_7_out, ~nor_3_out, in_12);  // NOR_Gate
  or or_1 (out_13, and_1_out, x3, and_2_out);
  not not_3 (out_14, nor_8_out);
  nor nor_8 (nor_8_out, nor_6_out, in_5, nor_4_out);
  not not_4 (out_15, nor_9_out);
  nor nor_9 (nor_9_out, nor_7_out, in_9, nor_5_out);
endmodule
