// Logisim project OpCode.circ as structural Verilog: 7 circuits, main circuit main
module main (
  input  [2:0] OpCode,
  input  A3,
  input  A2,
  input  A1,
  input  A0,
  input  B3,
  input  B2,
  input  B1,
  input  B0,
  output f4,
  output f3,
  output f2,
  output f1,
  output f0
);

  wire alu_2_cout, alu_3_cout, alu_4_cout, cin_1_cout;

  ALU alu_1 (.f(f3), .OpCode(OpCode), .Cout(f4), .B(B3), .A(A3), .Cin(alu_2_cout));
  ALU alu_2 (.f(f2), .OpCode(OpCode), .Cout(alu_2_cout), .B(B2), .A(A2), .Cin(alu_3_cout));
  ALU alu_3 (.f(f1), .OpCode(OpCode), .Cout(alu_3_cout), .B(B1), .A(A1), .Cin(alu_4_cout));
  ALU alu_4 (.f(f0), .OpCode(OpCode), .Cout(alu_4_cout), .B(B0), .A(A0), .Cin(cin_1_cout));
  Cin cin_1 (.OpCode(OpCode), .Cout(cin_1_cout));

  // Notes on the sheet:
  //   010
  //   100
  //   101
  //   110
  //   111
  //   Op Code
  //   A Plus B
  //   000
  //   001
  //   A Plus 1
  //   A Minus B
  //   011
  //   A Minus 1
  //   A XOR B
  //   A'
  //   A OR B
  //   A AND B
endmodule

module ALU (
  input  [2:0] OpCode,
  input  A,
  input  B,
  input  Cin,
  output f,
  output Cout
);

  wire add_1_cout, add_1_s, and_1_out, decrement_1_cout, decrement_1_f, increment_1_cout, increment_1_f,
       not_1_out, or_1_out, subtract_1_bout, subtract_1_f, xor_1_out;

  add add_1 (.A(A), .B(B), .Cin(Cin), .S(add_1_s), .Cout(add_1_cout));
  increment increment_1 (.A(A), .Cin(Cin), .f(increment_1_f), .Cout(increment_1_cout));
  Subtract subtract_1 (.X(A), .Y(B), .Bin(Cin), .f(subtract_1_f), .Bout(subtract_1_bout));
  decrement decrement_1 (.A(A), .Cin(Cin), .f(decrement_1_f), .Cout(decrement_1_cout));
  xor xor_1 (xor_1_out, A, B);
  not not_1 (not_1_out, A);
  or or_1 (or_1_out, A, B);
  and and_1 (and_1_out, A, B);
  Multiplexer #(.select(3), .enable("false")) multiplexer_1 (
    .in0(add_1_s), .in1(increment_1_f), .in2(subtract_1_f), .in3(decrement_1_f), .in4(xor_1_out),
    .in5(not_1_out), .in6(or_1_out), .in7(and_1_out), .out(f), .sel(OpCode));
  Multiplexer #(.select(3), .enable("false")) multiplexer_2 (
    .in0(add_1_cout), .in1(increment_1_cout), .in2(subtract_1_bout), .in3(decrement_1_cout), .in4(1'b0),
    .in5(1'b0), .in6(1'b0), .in7(1'b0), .out(Cout), .sel(OpCode));
endmodule

module add (
  input  A,
  input  B,
  input  Cin,
  output S,
  output Cout
);

  wire and_1_out, and_2_out, and_3_out, xor_1_out;

  xor xor_1 (xor_1_out, A, B);
  and and_1 (and_1_out, A, B);
  and and_2 (and_2_out, A, Cin);
  and and_3 (and_3_out, B, Cin);
  xor xor_2 (S, xor_1_out, Cin);
  or or_1 (Cout, and_1_out, and_2_out, and_3_out);
endmodule

module increment (
  input  A,
  input  Cin,
  output f,
  output Cout
);

  xor xor_1 (f, A, Cin);
  and and_1 (Cout, A, Cin);
endmodule

module Subtract (
  input  X,
  input  Y,
  input  Bin,
  output f,
  output Bout
);

  wire and_1_out, and_2_out, and_3_out;

  ExactlyOne xor_1 (.out(f), .in0(X), .in1(Y), .in2(Bin));
  and and_1 (and_1_out, ~X, Bin);  // AND_Gate
  and and_2 (and_2_out, ~X, Y);  // AND_Gate
  and and_3 (and_3_out, Y, Bin);
  or or_1 (Bout, and_1_out, and_2_out, and_3_out);
endmodule

module decrement (
  input  A,
  input  Cin,
  output f,
  output Cout
);

  xor xor_1 (f, A, Cin);
  and and_1 (Cout, ~A, Cin);  // AND_Gate
endmodule

module Cin (
  input  [2:0] OpCode,
  output Cout
);

  wire and_1_out, and_2_out, and_3_out, and_4_out;

  and and_1 (and_1_out, OpCode[0], ~OpCode[1]);  // AND_Gate
  and and_2 (and_2_out, OpCode[0], OpCode[1]);
  and and_3 (and_3_out, and_1_out, ~OpCode[2]);  // AND_Gate
  and and_4 (and_4_out, and_2_out, ~OpCode[2]);  // AND_Gate
  or or_1 (Cout, and_3_out, and_4_out);

  // Notes on the sheet:
  //   Handles Increment and Decrement 011 and 001
endmodule
