// Logisim project SR-Latch.circ as structural Verilog: 1 circuit, main circuit main
module main (
  input  R,
  input  S,
  input  R_2,
  input  S_2,
  output out_5,
  output out_6
);

  wire and_1_out, nand_1_out;

  and and_1 (and_1_out, ~out_5, ~R);  // AND_Gate
  nand nand_1 (nand_1_out, out_6, R_2);
  nor nor_1 (out_5, and_1_out, S);
  or or_1 (out_6, ~nand_1_out, ~S_2);  // OR_Gate
endmodule
