// Logisim project Subtractor.circ as structural Verilog: 2 circuits, main circuit main
module main (
  input  A0,
  input  B0,
  input  A1,
  input  B1,
  input  A2,
  input  B2,
  output f0,
  output f1,
  output f2
);

  wire fs_1_bout, fs_2_bout;

  FS fs_1 (.X(A0), .Y(B0), .Bin(1'b0), .f(f0), .Bout(fs_1_bout));
  FS fs_2 (.X(A1), .Y(B1), .Bin(fs_1_bout), .f(f1), .Bout(fs_2_bout));
  FS fs_3 (.X(A2), .Y(B2), .Bin(fs_2_bout), .f(f2));  // open: Bout
endmodule

module FS (
  input  X,
  input  Y,
  input  Bin,
  output f,
  output Bout
);

  wire and_1_out, and_2_out, and_3_out;

  ExactlyOne xor_1 (.out(f), .in0(X), .in1(Y), .in2(Bin));
  and and_1 (and_1_out, ~X, Bin);  // AND_Gate
  and and_2 (and_2_out, ~X, Y);  // AND_Gate
  and and_3 (and_3_out, Y, Bin);
  or or_1 (Bout, and_1_out, and_2_out, and_3_out);
endmodule
