// Logisim project Two's_complement.circ as structural Verilog: 1 circuit, main circuit main
module main (
  input  A0,
  input  A1,
  input  A2,
  input  A3,
  output F0,
  output F1,
  output F2,
  output F3
);

  wire and_1_out, and_2_out, not_1_out, not_2_out, not_3_out, not_4_out;

  not not_1 (not_1_out, A1);
  not not_2 (not_2_out, A2);
  not not_3 (not_3_out, A3);
  not not_4 (not_4_out, A0);
  xor xor_1 (F1, not_4_out, not_1_out);
  and and_1 (and_1_out, not_4_out, not_1_out);
  xor xor_2 (F2, and_1_out, not_2_out);
  and and_2 (and_2_out, and_1_out, not_2_out);
  xor xor_3 (F3, and_2_out, not_3_out);

  assign F0 = A0;
endmodule
