// Logisim project comparator.circ as structural Verilog: 3 circuits, main circuit main
module main (
  input  A3,
  input  A2,
  input  A1,
  input  A0,
  input  B3,
  input  B2,
  input  B1,
  input  B0,
  input  A3_2,
  input  A2_2,
  input  A1_2,
  input  A0_2,
  input  B3_2,
  input  B2_2,
  input  B1_2,
  input  B0_2,
  output A_GT_B,
  output A_LT_B,
  output A_EQ_B,
  output A_GT_B_2,
  output A_LT_B_2,
  output A_EQ_B_2
);

  wire compare_slice_2_eqout, compare_slice_2_gtout, compare_slice_2_ltout, compare_slice_3_eqout,
       compare_slice_3_gtout, compare_slice_3_ltout, compare_slice_4_eqout, compare_slice_4_gtout,
       compare_slice_4_ltout, compare_slice_min_2_gtout, compare_slice_min_2_ltout,
       compare_slice_min_3_gtout, compare_slice_min_3_ltout, compare_slice_min_4_gtout,
       compare_slice_min_4_ltout;

  nor nor_1 (A_EQ_B_2, A_GT_B_2, A_LT_B_2);
  Compare_slice compare_slice_1 (
    .A(A3), .B(B3), .GTin(compare_slice_2_gtout), .LTin(compare_slice_2_ltout), .EQin(compare_slice_2_eqout),
    .GTout(A_GT_B), .LTout(A_LT_B), .EQout(A_EQ_B));
  Compare_slice compare_slice_2 (
    .A(A2), .B(B2), .GTin(compare_slice_3_gtout), .LTin(compare_slice_3_ltout), .EQin(compare_slice_3_eqout),
    .GTout(compare_slice_2_gtout), .LTout(compare_slice_2_ltout), .EQout(compare_slice_2_eqout));
  Compare_slice_Min compare_slice_min_1 (
    .A(A3_2), .B(B3_2), .GTin(compare_slice_min_2_gtout), .LTin(compare_slice_min_2_ltout), .GTout(A_GT_B_2),
    .LTout(A_LT_B_2));
  Compare_slice compare_slice_3 (
    .A(A1), .B(B1), .GTin(compare_slice_4_gtout), .LTin(compare_slice_4_ltout), .EQin(compare_slice_4_eqout),
    .GTout(compare_slice_3_gtout), .LTout(compare_slice_3_ltout), .EQout(compare_slice_3_eqout));
  Compare_slice_Min compare_slice_min_2 (
    .A(A2_2), .B(B2_2), .GTin(compare_slice_min_3_gtout), .LTin(compare_slice_min_3_ltout),
    .GTout(compare_slice_min_2_gtout), .LTout(compare_slice_min_2_ltout));
  Compare_slice_Min compare_slice_min_3 (
    .A(A1_2), .B(B1_2), .GTin(compare_slice_min_4_gtout), .LTin(compare_slice_min_4_ltout),
    .GTout(compare_slice_min_3_gtout), .LTout(compare_slice_min_3_ltout));
  Compare_slice compare_slice_4 (
    .A(A0), .B(B0), .GTin(1'b0), .LTin(1'b0), .EQin(1'b1), .GTout(compare_slice_4_gtout),
    .LTout(compare_slice_4_ltout), .EQout(compare_slice_4_eqout));
  Compare_slice_Min compare_slice_min_4 (
    .A(A0_2), .B(B0_2), .GTin(1'b0), .LTin(1'b0), .GTout(compare_slice_min_4_gtout),
    .LTout(compare_slice_min_4_ltout));
endmodule

module Compare_slice (
  input  A,
  input  B,
  input  GTin,
  input  LTin,
  input  EQin,
  output GTout,
  output LTout,
  output EQout
);

  wire and_1_out, and_2_out, and_3_out, and_4_out, and_5_out, and_6_out, and_7_out, and_8_out, not_1_out,
       not_2_out, not_3_out, not_4_out, not_5_out, not_6_out;

  not not_1 (not_1_out, B);
  not not_2 (not_2_out, B);
  not not_3 (not_3_out, A);
  not not_4 (not_4_out, A);
  not not_5 (not_5_out, A);
  not not_6 (not_6_out, B);
  and and_1 (and_1_out, not_1_out, GTin);
  and and_2 (and_2_out, A, not_2_out);
  and and_3 (and_3_out, A, GTin);
  and and_4 (and_4_out, not_3_out, LTin);
  and and_5 (and_5_out, not_4_out, B);
  and and_6 (and_6_out, B, LTin);
  and and_7 (and_7_out, not_5_out, not_6_out, EQin);
  and and_8 (and_8_out, A, B, EQin);
  or or_1 (GTout, and_1_out, and_2_out, and_3_out);
  or or_2 (LTout, and_4_out, and_5_out, and_6_out);
  or or_3 (EQout, and_7_out, and_8_out);
endmodule

module Compare_slice_Min (
  input  A,
  input  B,
  input  GTin,
  input  LTin,
  output GTout,
  output LTout
);

  wire and_1_out, and_2_out, and_3_out, and_4_out, and_5_out, and_6_out, not_1_out, not_2_out, not_3_out,
       not_4_out;

  not not_1 (not_1_out, B);
  not not_2 (not_2_out, B);
  not not_3 (not_3_out, A);
  not not_4 (not_4_out, A);
  and and_1 (and_1_out, not_1_out, GTin);
  and and_2 (and_2_out, A, not_2_out);
  and and_3 (and_3_out, A, GTin);
  and and_4 (and_4_out, not_3_out, LTin);
  and and_5 (and_5_out, not_4_out, B);
  and and_6 (and_6_out, B, LTin);
  or or_1 (GTout, and_1_out, and_2_out, and_3_out);
  or or_2 (LTout, and_4_out, and_5_out, and_6_out);
endmodule
